// Digital circuit 74HC4060.dig as structural Verilog
module _74HC4060 (
  input  nCKin,
  input  CLR,
  input  VCC,
  input  GND,
  output Q12,
  output Q13,
  output Q14,
  output Q7,
  output Q8,
  output Q9,
  output Q10,
  output Q4,
  output Q5,
  output Q6,
  output CKout,
  output nCKout
);

  wire d_ff_as_1_nq, d_ff_as_2_nq, d_ff_as_3_nq, d_ff_as_4_nq, d_ff_as_5_nq, d_ff_as_6_nq, d_ff_as_7_nq,
       d_ff_as_8_nq, d_ff_as_9_nq, d_ff_as_10_nq, d_ff_as_11_nq, d_ff_as_12_nq, d_ff_as_13_nq, d_ff_as_14_nq,
       not_1_out, not_2_out, not_4_out;

  PowerSupply powersupply_1 (.VDD(VCC), .GND(GND));
  not not_1 (not_1_out, CLR);
  or or_1 (CKout, ~nCKin, ~not_1_out);  // Or
  not not_2 (not_2_out, not_1_out);
  not not_3 (nCKout, CKout);
  not not_4 (not_4_out, nCKout);
  D_FF_AS d_ff_as_1 (.Set(1'b0), .D(d_ff_as_1_nq), .C(not_4_out), .Clr(not_2_out), .nQ(d_ff_as_1_nq));  // open: Q
  D_FF_AS d_ff_as_2 (.Set(1'b0), .D(d_ff_as_2_nq), .C(d_ff_as_1_nq), .Clr(not_2_out), .nQ(d_ff_as_2_nq));  // open: Q
  D_FF_AS d_ff_as_3 (.Set(1'b0), .D(d_ff_as_3_nq), .C(d_ff_as_2_nq), .Clr(not_2_out), .nQ(d_ff_as_3_nq));  // open: Q
  D_FF_AS d_ff_as_4 (.Set(1'b0), .D(d_ff_as_4_nq), .C(d_ff_as_3_nq), .Clr(not_2_out), .nQ(d_ff_as_4_nq));  // open: Q
  not not_5 (Q4, d_ff_as_4_nq);
  D_FF_AS d_ff_as_5 (.Set(1'b0), .D(d_ff_as_5_nq), .C(d_ff_as_4_nq), .Clr(not_2_out), .nQ(d_ff_as_5_nq));  // open: Q
  not not_6 (Q5, d_ff_as_5_nq);
  D_FF_AS d_ff_as_6 (.Set(1'b0), .D(d_ff_as_6_nq), .C(d_ff_as_5_nq), .Clr(not_2_out), .nQ(d_ff_as_6_nq));  // open: Q
  not not_7 (Q6, d_ff_as_6_nq);
  D_FF_AS d_ff_as_7 (.Set(1'b0), .D(d_ff_as_7_nq), .C(d_ff_as_6_nq), .Clr(not_2_out), .nQ(d_ff_as_7_nq));  // open: Q
  not not_8 (Q7, d_ff_as_7_nq);
  D_FF_AS d_ff_as_8 (.Set(1'b0), .D(d_ff_as_8_nq), .C(d_ff_as_7_nq), .Clr(not_2_out), .nQ(d_ff_as_8_nq));  // open: Q
  not not_9 (Q8, d_ff_as_8_nq);
  D_FF_AS d_ff_as_9 (.Set(1'b0), .D(d_ff_as_9_nq), .C(d_ff_as_8_nq), .Clr(not_2_out), .nQ(d_ff_as_9_nq));  // open: Q
  not not_10 (Q9, d_ff_as_9_nq);
  D_FF_AS d_ff_as_10 (.Set(1'b0), .D(d_ff_as_10_nq), .C(d_ff_as_9_nq), .Clr(not_2_out), .nQ(d_ff_as_10_nq));  // open: Q
  not not_11 (Q10, d_ff_as_10_nq);
  D_FF_AS d_ff_as_11 (
    .Set(1'b0), .D(d_ff_as_11_nq), .C(d_ff_as_10_nq), .Clr(not_2_out), .nQ(d_ff_as_11_nq));  // open: Q
  D_FF_AS d_ff_as_12 (
    .Set(1'b0), .D(d_ff_as_12_nq), .C(d_ff_as_11_nq), .Clr(not_2_out), .nQ(d_ff_as_12_nq));  // open: Q
  not not_12 (Q12, d_ff_as_12_nq);
  D_FF_AS d_ff_as_13 (
    .Set(1'b0), .D(d_ff_as_13_nq), .C(d_ff_as_12_nq), .Clr(not_2_out), .nQ(d_ff_as_13_nq));  // open: Q
  not not_13 (Q13, d_ff_as_13_nq);
  D_FF_AS d_ff_as_14 (
    .Set(1'b0), .D(d_ff_as_14_nq), .C(d_ff_as_13_nq), .Clr(not_2_out), .nQ(d_ff_as_14_nq));  // open: Q
  not not_14 (Q14, d_ff_as_14_nq);

  // Notes on the sheet:
  //   nCKin: pin 11
  //   CLR: pin 12
  //   Q12: pin 1
  //   Q13: pin 2
  //   Q14: pin 3
  //   Q7: pin 6
  //   Q8: pin 14
  //   Q9: pin 13
  //   Q10: pin 15
  //   Q4: pin 7
  //   Q5: pin 5
  //   Q6: pin 4
  //   CKout: pin 10
  //   nCKout: pin 9
  //   VCC: pin 16, default 1
  //   GND: pin 8
endmodule
