// Digital circuit BS_TESTBED_04.dig as structural Verilog
module BS_TESTBED_04 (
  input  clk,
  input  IR4,
  input  IR5,
  input  IR6,
  input  in_11,
  output nLDB,
  output GCLK,
  output T0,
  output nRST,
  output nB,
  output CLR_AC,
  output PC_CLK
);

  wire ALU_CARRY, ALU_SUM, and_2_out, Aout, Bout, BUS0, BUS1, BUS2, BUS3, BUS4, BUS5, BUS6, BUS7,
       button_1_out, button_2_out, button_3_out, button_4_out, button_5_out, button_6_out, button_7_out,
       button_8_out, button_9_out, button_10_out, button_11_out, button_12_out, button_13_out, button_14_out,
       button_15_out, button_16_out, button_17_out, Cin, D0, D1, D2, D3, D4, D5, D6, D7, D8, D9, D10, D11,
       D12, D13, D14, D15, d_ff_1_nq, d_ff_2_nq, d_ff_3_nq, d_ff_4_nq, d_ff_5_nq, d_ff_6_nq, d_ff_7_nq,
       d_ff_8_nq, d_ff_9_nq, d_ff_10_nq, d_ff_11_nq, d_ff_12_nq, diodeforward_1_out, Fout, I0, I1, IC16_2_nq,
       IC16_nq, IC17_2_nq, IC17_nq, nADD, nand_5_out, nCRES, nCSET, nCSup, nJMP, nLOAD, nOR, not_1_out,
       nRESET, nST, nSUB, nT1, nT17, nT18, nXOR, PC0, PC1, PC2, PC3, PC4, PC5, PC6, PC7, PC8, PC9, PC10,
       PC11, PC12, PC13, PC14, PC15, PC_CARRYIN, PC_CARRYOUT, PC_in, PC_SUM, PCout, QD, RCO, RST, RUN, SETC,
       T17, T18, U3_pin14, U4_pin9, U14_pin14, U15_pin3, U15_pin6, U15_pin13, U22_pin9, Y0, ZERO;
  wire [2:0] U9_pin12;
  wire [3:0] d_ff_3_q, IC17_2_q;

  Reset reset_1 (.out(nRESET));
  Monoflop monoflop_1 (.C(button_1_out), .R(1'b0), .Q(RUN));  // open: nQ
  Button button_1 (.out(button_1_out));
  _74138 U10 (
    .pin1(IR4), .pin2(IR5), .pin3(IR6), .pin4(1'b0), .pin5(1'b0), .pin6(1'b1), .pin7(nJMP), .pin8(1'b0),
    .pin9(nST), .pin10(nSUB), .pin11(nADD), .pin12(nXOR), .pin13(nOR), .pin14(I0), .pin15(nLOAD), .pin16(1'b1));
  not not_1 (not_1_out, QD);
  LED led_1 (.in(d_ff_3_q[3]));
  D_FF IC17 (.D(IC17_nq), .C(button_2_out), .Q(d_ff_3_q[3]), .nQ(IC17_nq));
  and and_1 (GCLK, 1'b1, not_1_out, PC_CLK);
  LED led_2 (.in(d_ff_3_q[2]));
  D_FF d_ff_1 (.D(d_ff_1_nq), .C(button_3_out), .Q(d_ff_3_q[2]), .nQ(d_ff_1_nq));
  Button button_2 (.out(button_2_out));
  LED led_3 (.in(d_ff_3_q[1]));
  D_FF d_ff_2 (.D(d_ff_2_nq), .C(button_4_out), .Q(d_ff_3_q[1]), .nQ(d_ff_2_nq));
  Button button_3 (.out(button_3_out));
  _74595 U3 (
    .pin1(PC6), .pin2(PC5), .pin3(PC4), .pin4(PC3), .pin5(PC2), .pin6(PC1), .pin7(PC0), .pin8(1'b0),
    .pin9(PCout), .pin10(nRESET), .pin11(PC_CLK), .pin12(nT17), .pin13(1'b0), .pin14(U3_pin14), .pin15(PC7),
    .pin16(1'b1));
  LED led_4 (.in(d_ff_3_q[0]));
  D_FF d_ff_3 (.D(d_ff_3_nq), .C(button_5_out), .Q(d_ff_3_q[0]), .nQ(d_ff_3_nq));
  Button button_4 (.out(button_4_out));
  xor xor_1 (nB, 1'b1, nSUB);
  xor xor_2 (Y0, 1'b1, nLOAD);
  LED led_5 (.in(IC17_2_q[3]));
  D_FF d_ff_4 (.D(d_ff_4_nq), .C(button_6_out), .Q(IC17_2_q[3]), .nQ(d_ff_4_nq));
  Button button_5 (.out(button_5_out));
  LED led_6 (.in(IC17_2_q[2]));
  D_FF d_ff_5 (.D(d_ff_5_nq), .C(button_7_out), .Q(IC17_2_q[2]), .nQ(d_ff_5_nq));
  Button button_6 (.out(button_6_out));
  nand nand_1 (nCSup, T0, nSUB);
  nand nand_2 (nCSET, nB, SETC);
  nand nand_3 (I1, I0, nOR);
  nand nand_4 (CLR_AC, T0, Y0);
  and and_2 (and_2_out, I0, nOR, nXOR);
  LED led_7 (.in(IC17_2_q[1]));
  D_FF d_ff_6 (.D(d_ff_6_nq), .C(button_8_out), .Q(IC17_2_q[1]), .nQ(d_ff_6_nq));
  Button button_7 (.out(button_7_out));
  _74595 U2 (
    .pin1(PC14), .pin2(PC13), .pin3(PC12), .pin4(PC11), .pin5(PC10), .pin6(PC9), .pin7(PC8), .pin8(1'b0),
    .pin9(U3_pin14), .pin10(nRESET), .pin11(PC_CLK), .pin12(nT17), .pin13(1'b0), .pin14(PC_in), .pin15(PC15),
    .pin16(1'b1));
  LED led_8 (.in(IC17_2_q[0]));
  D_FF IC17_2 (.D(IC17_2_nq), .C(button_9_out), .Q(IC17_2_q[0]), .nQ(IC17_2_nq));
  Button button_8 (.out(button_8_out));
  and and_3 (nCRES, 1'b1, and_2_out, nCSup);
  Seven_Seg_Hex seven_seg_hex_1 (.d(d_ff_3_q), .dp(1'b0));
  Button button_9 (.out(button_9_out));
  Seven_Seg_Hex seven_seg_hex_2 (.d(IC17_2_q), .dp(1'b0));
  LED led_9 (.in(D7));
  D_FF IC16 (.D(IC16_nq), .C(button_10_out), .Q(D7), .nQ(IC16_nq));
  Button button_10 (.out(button_10_out));
  Seven_Seg_Hex seven_seg_hex_3 (.d({PC15, PC14, PC13, PC12}), .dp(1'b0));
  LED led_10 (.in(D6));
  D_FF d_ff_7 (.D(d_ff_7_nq), .C(button_11_out), .Q(D6), .nQ(d_ff_7_nq));
  Button button_11 (.out(button_11_out));
  _74595 U22 (
    .pin1(BUS6), .pin2(BUS5), .pin3(BUS4), .pin4(BUS3), .pin5(BUS2), .pin6(BUS1), .pin7(BUS0), .pin8(1'b0),
    .pin9(U22_pin9), .pin10(CLR_AC), .pin11(GCLK), .pin12(nT17), .pin13(1'b1), .pin14(Fout), .pin15(BUS7),
    .pin16(1'b1));
  Seven_Seg_Hex seven_seg_hex_4 (.d({PC11, PC10, PC9, PC8}), .dp(1'b0));
  LED led_11 (.in(D5));
  D_FF d_ff_8 (.D(d_ff_8_nq), .C(button_12_out), .Q(D5), .nQ(d_ff_8_nq));
  Button button_12 (.out(button_12_out));
  Seven_Seg_Hex seven_seg_hex_5 (.d({PC7, PC6, PC5, PC4}), .dp(1'b0));
  LED led_12 (.in(D4));
  D_FF d_ff_9 (.D(d_ff_9_nq), .C(button_13_out), .Q(D4), .nQ(d_ff_9_nq));
  Button button_13 (.out(button_13_out));
  Seven_Seg_Hex seven_seg_hex_6 (.d({PC3, PC2, PC1, PC0}), .dp(1'b0));
  LED led_13 (.in(D3));
  D_FF d_ff_10 (.D(d_ff_10_nq), .C(button_14_out), .Q(D3), .nQ(d_ff_10_nq));
  Button button_14 (.out(button_14_out));
  DiodeForward diodeforward_1 (.in(BUS7), .out(diodeforward_1_out));
  DiodeForward diodeforward_2 (.in(BUS6), .out(diodeforward_1_out));
  DiodeForward diodeforward_3 (.in(BUS5), .out(diodeforward_1_out));
  DiodeForward diodeforward_4 (.in(BUS4), .out(diodeforward_1_out));
  DiodeForward diodeforward_5 (.in(BUS3), .out(diodeforward_1_out));
  DiodeForward diodeforward_6 (.in(BUS2), .out(diodeforward_1_out));
  DiodeForward diodeforward_7 (.in(BUS1), .out(diodeforward_1_out));
  DiodeForward diodeforward_8 (.in(BUS0), .out(diodeforward_1_out));
  LED led_14 (.in(D2));
  D_FF d_ff_11 (.D(d_ff_11_nq), .C(button_15_out), .Q(D2), .nQ(d_ff_11_nq));
  Button button_15 (.out(button_15_out));
  Seven_Seg_Hex seven_seg_hex_7 (.d({BUS7, BUS6, BUS5, BUS4}), .dp(1'b0));
  PullDown pulldown_1 (.out(diodeforward_1_out));
  LED led_15 (.in(D1));
  D_FF d_ff_12 (.D(d_ff_12_nq), .C(button_16_out), .Q(D1), .nQ(d_ff_12_nq));
  Button button_16 (.out(button_16_out));
  Seven_Seg_Hex seven_seg_hex_8 (.d({BUS3, BUS2, BUS1, BUS0}), .dp(1'b0));
  xor xor_3 (ZERO, 1'b1, diodeforward_1_out);
  LED led_16 (.in(D0));
  D_FF IC16_2 (.D(IC16_2_nq), .C(button_17_out), .Q(D0), .nQ(IC16_2_nq));
  Button button_17 (.out(button_17_out));
  LED led_17 (.in(ZERO));
  Seven_Seg_Hex seven_seg_hex_9 (.d({D7, D6, D5, D4}), .dp(1'b0));
  Seven_Seg_Hex seven_seg_hex_10 (.d({D3, D2, D1, D0}), .dp(1'b0));
  _74299 U17 (
    .pin1(in_11), .pin2(RST), .pin3(RST), .pin4(BUS6), .pin5(BUS4), .pin6(BUS2), .pin7(BUS0), .pin8(Aout),
    .pin9(CLR_AC), .pin10(1'b0), .pin11(1'b0), .pin12(GCLK), .pin13(BUS1), .pin14(BUS3), .pin15(BUS5),
    .pin16(BUS7), .pin18(Fout), .pin19(1'b1), .pin20(1'b1));  // open: pin17
  _74283 U14 (
    .pin1(PC_CARRYOUT), .pin2(1'b0), .pin3(1'b0), .pin4(PC_SUM), .pin5(1'b0), .pin6(PCout),
    .pin7(PC_CARRYIN), .pin8(1'b0), .pin9(ALU_CARRY), .pin10(ALU_SUM), .pin11(Cin), .pin12(Aout),
    .pin14(U14_pin14), .pin15(1'b1), .pin16(1'b1));  // open: pin13
  nand nand_5 (nand_5_out, clk, clk);
  nand nand_6 (RST, nT1, nRST);
  nand nand_7 (nRST, RST, nT17);
  nand nand_8 (PC_CLK, nand_5_out, RST);
  xor xor_4 (U14_pin14, Bout, nB);
  PullDown pulldown_2 (.out(Fout));
  _74161 U9 (
    .pin1(RST), .pin2(clk), .pin3(1'b0), .pin4(1'b0), .pin5(1'b0), .pin6(1'b0), .pin7(1'b1), .pin8(1'b0),
    .pin9(1'b1), .pin10(1'b1), .pin11(QD), .pin12(U9_pin12[2]), .pin13(U9_pin12[1]), .pin14(U9_pin12[0]),
    .pin15(RCO), .pin16(1'b1));
  _74126 U15 (
    .pin1(I0), .pin2(ALU_SUM), .pin3(U15_pin3), .pin4(I1), .pin5(ALU_CARRY), .pin6(U15_pin6), .pin7(1'b0),
    .pin8(PC_in), .pin9(PC_SUM), .pin10(nJMP), .pin11(PC_in), .pin12(Bout), .pin13(U15_pin13), .pin14(1'b1));
  DiodeForward diodeforward_9 (.in(U15_pin3), .out(Fout));
  DiodeForward diodeforward_10 (.in(U15_pin6), .out(Fout));
  _74165 U4 (
    .pin1(nLDB), .pin2(PC_CLK), .pin3(D11), .pin4(D10), .pin5(D9), .pin6(D8), .pin8(1'b0), .pin9(U4_pin9),
    .pin10(1'b0), .pin11(D15), .pin12(D14), .pin13(D13), .pin14(D12), .pin15(1'b0), .pin16(1'b1));  // open: pin7
  not not_2 (U15_pin13, nJMP);
  Seven_Seg_Hex seven_seg_hex_11 (.d({QD, U9_pin12}), .dp(1'b0));
  _74165 U5 (
    .pin1(nLDB), .pin2(PC_CLK), .pin3(D3), .pin4(D2), .pin5(D1), .pin6(D0), .pin8(1'b0), .pin9(Bout),
    .pin10(1'b0), .pin11(D7), .pin12(D6), .pin13(D5), .pin14(D4), .pin15(U4_pin9), .pin16(1'b1));  // open: pin7
  _7474 U16 (
    .pin1(nCRES), .pin2(ALU_CARRY), .pin3(GCLK), .pin4(nCSET), .pin5(Cin), .pin7(1'b0), .pin9(PC_CARRYIN),
    .pin10(nLDB), .pin11(GCLK), .pin12(PC_CARRYOUT), .pin13(1'b1), .pin14(1'b1));  // open: pin6, pin8
  _74175 U9_2 (
    .pin1(nRESET), .pin2(T17), .pin3(nT17), .pin4(RCO), .pin5(T17), .pin6(nT18), .pin7(T18), .pin8(1'b0),
    .pin9(clk), .pin10(T0), .pin11(nLDB), .pin12(RUN), .pin13(T0), .pin14(nT1), .pin15(SETC), .pin16(1'b1));

  // Other names for the same wires on the sheet: nCLR_AC = CLR_AC; nBLOAD = nLDB; nT0 = nLDB; RCLK = nT17;
  //   nY0 = nLOAD; nAND = I0; nY1 = I0; nY2 = nOR; nY3 = nXOR; nY4 = nADD; nY5 = nSUB; nY6 = nST; nY7 = nJMP;
  //   S0 = in_11; T1 = SETC

  // Notes on the sheet:
  //   clk: Hz: 200
  //   BIT SERIAL TESTBED 04
  //   0    0    0 LOAD
  //   0    0    1 AND
  //   0   1   0 OR
  //   0    1   1 XOR
  //   1    0    0 ADD
  //   1   0    1 SUB
  //   0    0    0 STORE
  //   0    0    1 JUMP
  //   STEP/RUN
  //   INSTRUCTION DECODER
  //   Instruction Decode
  //   PROGRAM COUNTER
  //   U19
  //   U11C
  //   ENTER H
  //   U12B
  //   U12C
  //   Suppress Carry
  //   U13
  //   74HC00
  //   74HC11
  //   U11A
  //   U11B
  //   Data Input
  //   SPI INPUT REGISTER
  //   ROM ADDRESS
  //   ENTER L
  //   ACCUMULATOR
  //   DATA BUS
  //   U12A
  //   ZERO
  //   CLOCK SEQUENCER
  //   ALU & PC INCREMENTER
  //   U7
  //   PC INC / ALU
  //   U12D
  //   PC / ALU MUX
  //   B-REGISTER HIGH
  //   # Clock
  //   ALU Carry FF
  //   B-REGISTER LOW
  //   SEQUENCER FFs
  //   PC Carry FF
endmodule
