// Digital circuit PC_demonstrator.dig as structural Verilog
module PC_demonstrator (
  input  clk,
  input  in_2,
  input  in_3,
  output T0,
  output nLOAD,
  output GCLK,
  output nRES,
  output nRCO,
  output RST,
  output _8_CLK,
  output nQD,
  output PCOUT
);

  wire A0, A1, A2, A3, A4, A5, A6, A7, A8, A9, A10, A11, A12, A13, A14, A15, IX, nand_1_out, nand_3_out,
       nand_5_out, nand_6_out, nand_7_out, nand_8_out, nCLRPC, not_3_out, not_5_out, PC_Cin, PCin, RCO,
       U16_pin9, xor_1_out;
  wire [3:0] U7_pin11;

  _74595 U16 (
    .pin1(A14), .pin2(A13), .pin3(A12), .pin4(A11), .pin5(A10), .pin6(A9), .pin7(A8), .pin8(1'b0),
    .pin9(U16_pin9), .pin10(nCLRPC), .pin11(GCLK), .pin12(nLOAD), .pin13(1'b0), .pin14(PCin), .pin15(A15),
    .pin16(1'b1));
  not not_1 (nRCO, RCO);
  _74595 U17 (
    .pin1(A6), .pin2(A5), .pin3(A4), .pin4(A3), .pin5(A2), .pin6(A1), .pin7(A0), .pin8(1'b0), .pin9(PCOUT),
    .pin10(nCLRPC), .pin11(GCLK), .pin12(nLOAD), .pin13(1'b0), .pin14(U16_pin9), .pin15(A7), .pin16(1'b1));
  nand nand_1 (nand_1_out, clk, clk);
  nand nand_2 (RST, nRES, nand_3_out);
  nand nand_3 (nand_3_out, RST, nLOAD);
  Seven_Seg_Hex seven_seg_hex_1 (.d({A15, A14, A13, A12}), .dp(1'b0));
  nand nand_4 (GCLK, nand_1_out, RST);
  Seven_Seg_Hex seven_seg_hex_2 (.d({A11, A10, A9, A8}), .dp(1'b0));
  Seven_Seg_Hex seven_seg_hex_3 (.d({A7, A6, A5, A4}), .dp(1'b0));
  Seven_Seg_Hex seven_seg_hex_4 (.d({A3, A2, A1, A0}), .dp(1'b0));
  nand nand_5 (nand_5_out, nQD, GCLK);
  _74161 U7 (
    .pin1(RST), .pin2(clk), .pin3(1'b0), .pin4(1'b0), .pin5(1'b0), .pin6(1'b0), .pin7(1'b1), .pin8(1'b0),
    .pin9(1'b1), .pin10(1'b1), .pin11(U7_pin11[3]), .pin12(U7_pin11[2]), .pin13(U7_pin11[1]),
    .pin14(U7_pin11[0]), .pin15(RCO), .pin16(1'b1));
  nand nand_6 (nand_6_out, PCOUT, PC_Cin);
  not not_2 (_8_CLK, nand_5_out);
  xor xor_1 (xor_1_out, PCOUT, PC_Cin);
  not not_3 (not_3_out, nand_6_out);
  not not_4 (nQD, U7_pin11[3]);
  nand nand_7 (nand_7_out, xor_1_out, not_5_out);
  not not_5 (not_5_out, in_2);
  nand nand_8 (nand_8_out, in_2, in_3);
  Seven_Seg_Hex seven_seg_hex_5 (.d(U7_pin11), .dp(1'b0));
  Reset reset_1 (.out(nCLRPC));
  nand nand_9 (PCin, nand_7_out, nand_8_out);
  D_FF_AS d_ff_as_1 (.Set(~nLOAD), .D(not_3_out), .C(GCLK), .Clr(~1'b1), .Q(PC_Cin));  // open: nQ
  _7474 _7474_1 (
    .pin1(nCLRPC), .pin2(IX), .pin3(clk), .pin4(1'b1), .pin6(nRES), .pin7(1'b0), .pin8(nLOAD), .pin9(IX),
    .pin10(1'b1), .pin11(clk), .pin12(RCO), .pin13(1'b1), .pin14(1'b1));  // open: pin5

  assign T0 = nLOAD;

  // Other names for the same wires on the sheet: Aout = in_3; nINC_LD = in_2; PCLD = in_2; nT0 = nLOAD

  // Notes on the sheet:
  //   clk: Hz: 20
  //   PROGRAM COUNTER
  //   Clock Sequencer
  //   Program Counter (Incrementer)
  //   U41A
  //   U24B
  //   U24C
  //   Carry is  set on timeslot T0 of an operation
  //   # Clock
  //   U31
  //   Carry FF
  //   U32A
endmodule
