// Digital circuit Program_Counter_Notes.dig as structural Verilog
module Program_Counter_Notes (
  input  clk,
  input  in_9,
  input  in_10,
  output nAC_EN,
  output nT0,
  output nT17,
  output PC_CLK,
  output nT18,
  output nT1,
  output RCO
);

  wire A0, A1, A2, A3, A4, A5, A6, A7, A8, A9, A10, A11, A12, A13, A14, A15, button_1_out, CLK1K, CLK1M,
       CLK2K, CLK4K, CLK16K, CLK32K, CLK64K, CLK125K, CLK250K, CLK500K, GCLK, JMP, LD, monoflop_1_nq,
       nand_2_out, nCLRPC, nQD, nRST, PC_CARRYIN, PC_CARRYOUT, PC_SUM, PCin, PCout, QD, RESET, reset_1_out,
       RUN, SETC, T17, T18, U2_pin9;
  wire [2:0] U8_pin14;

  Monoflop monoflop_1 (.C(button_1_out), .R(1'b0), .nQ(monoflop_1_nq));  // open: Q
  Button button_1 (.out(button_1_out));
  nand nand_1 (RUN, nT18, monoflop_1_nq);
  _74HC4060 U6 (
    .nCKin(clk), .CLR(RESET), .Q12(CLK4K), .Q13(CLK2K), .Q14(CLK1K), .Q7(CLK125K), .Q8(CLK64K), .Q9(CLK32K),
    .Q10(CLK16K), .Q4(CLK1M), .Q5(CLK500K), .Q6(CLK250K), .VCC(1'b1), .GND(1'b0));  // open: CKout, nCKout
  nand nand_2 (nand_2_out, clk, clk);
  nand nand_3 (nAC_EN, nT1, nRST);
  nand nand_4 (nRST, nAC_EN, nT17);
  nand nand_5 (PC_CLK, nand_2_out, nAC_EN);
  _7474 U16 (
    .pin1(1'b1), .pin2(1'b1), .pin3(1'b1), .pin4(1'b1), .pin7(1'b0), .pin9(PC_CARRYIN), .pin10(nT0),
    .pin11(PC_CLK), .pin12(PC_CARRYOUT), .pin13(1'b1), .pin14(1'b1));  // open: pin5, pin6, pin8
  _74161 U8 (
    .pin1(nAC_EN), .pin2(clk), .pin3(1'b0), .pin4(1'b0), .pin5(1'b0), .pin6(1'b0), .pin7(1'b1), .pin8(1'b0),
    .pin9(1'b1), .pin10(1'b1), .pin11(QD), .pin12(U8_pin14[2]), .pin13(U8_pin14[1]), .pin14(U8_pin14[0]),
    .pin15(RCO), .pin16(1'b1));
  _74595 U2 (
    .pin1(A14), .pin2(A13), .pin3(A12), .pin4(A11), .pin5(A10), .pin6(A9), .pin7(A8), .pin8(1'b0),
    .pin9(U2_pin9), .pin10(nCLRPC), .pin11(PC_CLK), .pin12(nT0), .pin13(1'b0), .pin14(PCin), .pin15(A15),
    .pin16(1'b1));
  Seven_Seg_Hex seven_seg_hex_1 (.d({QD, U8_pin14}), .dp(1'b0));
  _74283 U14 (
    .pin1(PC_CARRYOUT), .pin2(1'b0), .pin3(1'b0), .pin4(PC_SUM), .pin5(1'b0), .pin6(PCout),
    .pin7(PC_CARRYIN), .pin8(1'b0), .pin11(1'b1), .pin12(1'b1), .pin14(1'b1), .pin15(1'b1), .pin16(1'b1));  // open: pin9, pin10, pin13
  _74595 U3 (
    .pin1(A6), .pin2(A5), .pin3(A4), .pin4(A3), .pin5(A2), .pin6(A1), .pin7(A0), .pin8(1'b0), .pin9(PCout),
    .pin10(nCLRPC), .pin11(PC_CLK), .pin12(nT0), .pin13(1'b0), .pin14(U2_pin9), .pin15(A7), .pin16(1'b1));
  _74175 U9 (
    .pin1(nCLRPC), .pin2(T17), .pin3(nT17), .pin4(RCO), .pin5(T17), .pin6(nT18), .pin7(T18), .pin8(1'b0),
    .pin9(clk), .pin10(LD), .pin11(nT0), .pin12(RUN), .pin13(LD), .pin14(nT1), .pin15(SETC), .pin16(1'b1));
  _74126 U15 (
    .pin1(1'b1), .pin2(1'b1), .pin4(1'b1), .pin5(1'b1), .pin7(1'b0), .pin8(PCin), .pin9(PC_SUM),
    .pin10(in_9), .pin11(PCin), .pin12(in_10), .pin13(JMP), .pin14(1'b1));  // open: pin3, pin6
  Seven_Seg_Hex seven_seg_hex_2 (.d({A15, A14, A13, A12}), .dp(1'b0));
  Seven_Seg_Hex seven_seg_hex_3 (.d({A11, A10, A9, A8}), .dp(1'b0));
  Seven_Seg_Hex seven_seg_hex_4 (.d({A7, A6, A5, A4}), .dp(1'b0));
  Seven_Seg_Hex seven_seg_hex_5 (.d({A3, A2, A1, A0}), .dp(1'b0));
  not not_1 (JMP, in_9);
  and and_1 (GCLK, 1'b1, nQD, PC_CLK);
  Reset reset_1 (.out(reset_1_out));
  not not_2 (nQD, QD);
  not not_3 (RESET, reset_1_out);
  not not_4 (nCLRPC, RESET);

  // Other names for the same wires on the sheet: Bout = in_10; CLK16 = clk; nINC_LD = in_9; nJMP = in_9; PCLD = in_9;
  //   nLOAD = nT0; nLOADB = nT0; RCLK = nT0; nRESET = nCLRPC; RST = nAC_EN; T0 = LD; T1 = SETC

  // Notes on the sheet:
  //   clk: Hz: 1000
  //   TICK 8-BIT SERIAL COMPUTER - PROGRAM COUNTER DEMONSTRATOR
  //   PROGRAM COUNTER NOTES.
  //   Program Counter.
  //   The Program Counter consists of a 16-bit serial-in, parallel out shift register, a half adder, an 2-input multiplexer and a carry flipflop. However the design is somewhat convoluted and spread across 6 ICs.
  //   The following notes explain the design, and a simulation of the Program Counter circuit is available on the github repo.
  //   U2 and U3 (74HC595) form the 16-bit Program Counter.
  //   Output pins
  //   15		RMA15 (MSB)
  //   1		RMA14
  //   2		RMA13
  //   3		RMA12
  //   4		RMA11
  //   5		RMA10
  //   6		RMA9
  //   7		RMA8  (LSB)
  //   9		Serial Output to lower stage
  //   10		/CLR	Active LOW reset signal - check it goes low when RESET switch pressed
  //   11		PC_CLK  16-clock pulse burst - check for continuous clocking
  //   12		Outout Latch clock pulse - low going pulse, every 16th clock
  //   13     		 /PC_EN  Active LOW enable pin - should remain LOW
  //   14      		PC_IN  Serial Input 
  //   8		GND
  //   16 		3V3
  //   The Program Counter is connected to U12, U14 U15 and U16.
  //   U12 (74HC86) provides inversion of the !JMP signal.
  //   The left hand side of U14 (74HC283) provides a half adder to increment the PC by one, once per machine cycle (20 clocks).
  //   The right hand side of  U15 (74HC126) provides a 2-input multiplexer. The PC is either loaded with the current count, or if !JMP is LOW it is loaded with the value in the B-Register.
  //   U16 (74HC74) is a dual flipflop. The right-hand flipflop is used to hold any carry produced when adding 1 to the PC and adding it into the next half sum.
  //   Ensure continuity of:
  //   U2 (14) to U15 (8,11) 	*
  //   U2 (9) to U3 (14)  		*
  //   U3 (9) to U14(6) 		*
  //   U16 (12) to U14(1)		*
  //   U16 (11) to U7 (8)		new
  //   U16 (10) to U9(11)		new
  //   U16 (9) to U14(7)		*
  //   U14 (4) to U15(9)		*
  //   NOT INCLUDED ON PCB!
  //   PRESS TO START!
  //   /RUN
  //   TIMING SEQUENCER
  //   U7
  //   12
  //   13
  //   4
  //   5
  //   U7D
  //   U7A
  //   1
  //   2
  //   U7B
  //   10
  //   11
  //   3
  //   6
  //   Carry FF
  //   U7C
  //   9
  //   8
  //   PC Carry FF
  //   # Clock
  //   PC HALF-ADDER
  //   SEQUENCER FFs
  //   ALU FULL-ADDER
  //   INSTRUCTION DECODER
  //   PC / ALU MUX
  //   PROGRAM COUNTER
  //   U11
  //   74HC11
  //   U11C
  //   INVERTERS/RESET
  //   RESET
  //   U19
  //   U19B
  //   U19C
  //   U19D
endmodule
