// Digital circuit Step_1_TPG.dig as structural Verilog
module Step_1_TPG (
  input  clk,
  output nAC_EN,
  output GCLK,
  output nT0,
  output nT17,
  output PC_CLK,
  output nT18,
  output nT1,
  output RCO
);

  wire button_1_out, CLK1K, CLK1M, CLK2K, CLK4K, CLK16K, CLK32K, CLK64K, CLK125K, CLK250K, CLK500K, LD,
       monoflop_1_nq, nand_2_out, nQD, nRESET, nRST, QD, RESET, reset_1_out, RUN, SETC, T17, T18;
  wire [2:0] U8_pin14;

  Monoflop monoflop_1 (.C(button_1_out), .R(1'b0), .nQ(monoflop_1_nq));  // open: Q
  Button button_1 (.out(button_1_out));
  nand nand_1 (RUN, nT18, monoflop_1_nq);
  _74HC4060 U6 (
    .nCKin(clk), .CLR(RESET), .Q12(CLK4K), .Q13(CLK2K), .Q14(CLK1K), .Q7(CLK125K), .Q8(CLK64K), .Q9(CLK32K),
    .Q10(CLK16K), .Q4(CLK1M), .Q5(CLK500K), .Q6(CLK250K), .VCC(1'b1), .GND(1'b0));  // open: CKout, nCKout
  nand nand_2 (nand_2_out, clk, clk);
  nand nand_3 (nAC_EN, nT1, nRST);
  nand nand_4 (nRST, nAC_EN, nT17);
  nand nand_5 (PC_CLK, nand_2_out, nAC_EN);
  _74161 U8 (
    .pin1(nAC_EN), .pin2(clk), .pin3(1'b0), .pin4(1'b0), .pin5(1'b0), .pin6(1'b0), .pin7(1'b1), .pin8(1'b0),
    .pin9(1'b1), .pin10(1'b1), .pin11(QD), .pin12(U8_pin14[2]), .pin13(U8_pin14[1]), .pin14(U8_pin14[0]),
    .pin15(RCO), .pin16(1'b1));
  Seven_Seg_Hex seven_seg_hex_1 (.d({QD, U8_pin14}), .dp(1'b0));
  _74175 U9 (
    .pin1(nRESET), .pin2(T17), .pin3(nT17), .pin4(RCO), .pin5(T17), .pin6(nT18), .pin7(T18), .pin8(1'b0),
    .pin9(clk), .pin10(LD), .pin11(nT0), .pin12(RUN), .pin13(LD), .pin14(nT1), .pin15(SETC), .pin16(1'b1));
  and and_1 (GCLK, 1'b1, nQD, PC_CLK);
  Reset reset_1 (.out(reset_1_out));
  not not_1 (nQD, QD);
  not not_2 (RESET, reset_1_out);
  not not_3 (nRESET, RESET);

  // Other names for the same wires on the sheet: CLK16 = clk; nLOADB = nT0; RCLK = nT17; RST = nAC_EN; T0 = LD;
  //   T1 = SETC

  // Notes on the sheet:
  //   clk: Hz: 10
  //   TICK 8-BIT SERIAL COMPUTER - STAGE 1 CRYSTAL OSCILLATOR AND TIMING PULSE GENERATPR (TPG)
  //   BUILD STEPS - STAGE 1.
  //   1. Insert IC sockets into locations U6, U7, U8, U9, U11 and U19. Ensure the "notch" indicating pin 1 is correctly alighed with the notch on the pcb screenprint. All sockets lie flat on the pcb surface.
  //   2. Solder in the 100nF decoupling capacitors C6, C7, C8, C9, C11, C19 and C32. They should be fitted level with the top of the IC sockets.
  //   3. Solder in resistors R1, R2, R3, R4 ,R5, R6, R7, R8, and R9. Solder in 22pF capacitors C30 and C32, 16MHz crystal Q1, 2x10 pin male header J20  and "STEP" switch S13..
  //   4. Check underside of board for missed pins, poor solder joints or solder bridges. Put multimeter on ohms or continuity and check for no short between VCC and GND!
  //   5. Identify the ICs and gently press pins on bench to bend them parallel. Insert IC6 74HC4060.
  //   6. Apply 3.3V dc power to temporary power connector C1. With oscilliscope check for clean square wave signals on each of  LHS of J20. Fit jumper link across J20 pins 1 and 20
  //   7. Proceed to add the remainder of the  U7, U8, U9, U11 and U19.
  //   8. Using the scope, probe U9 for RCO, /T0, /T0, T1, /T1, T17, /T17, T18, /T18. Probe U19 for /QD, RESET and /RESET. Probe U11 for PC-CLK and GCLK.
  //   9. If all signals are present, proceed to the next stage. If any problems, bring the board out to "Debug Corner".
  //   NOT INCLUDED ON PCB!
  //   /RUN
  //   TIMING SEQUENCER
  //   U7
  //   12
  //   13
  //   4
  //   5
  //   U7D
  //   U7A
  //   1
  //   2
  //   U7B
  //   10
  //   11
  //   3
  //   6
  //   U7C
  //   9
  //   8
  //   # Clock
  //   SEQUENCER FFs
  //   INSTRUCTION DECODER
  //   U11
  //   74HC11
  //   U11C
  //   INVERTERS/RESET
  //   RESET
  //   U19
  //   U19B
  //   U19C
  //   U19D
endmodule
