// Digital circuit Step_3_Pi_Pico_Romulator.dig as structural Verilog
module Step_3_Pi_Pico_Romulator (
  input  clk,
  input  in_7,
  input  in_8,
  input  in_9,
  input  in_10,
  input  in_11,
  input  in_12,
  input  in_13,
  input  in_14,
  input  in_15,
  input  in_16,
  input  in_17,
  input  in_18,
  input  in_19,
  input  in_20,
  input  in_21,
  input  in_22,
  input  DATA,
  input  STB,
  input  SCLK,
  input  nRE,
  input  nRESET,
  input  _3V3,
  input  nEN,
  input  MOSI,
  input  STB_2,
  input  SCLK_2,
  input  GND,
  output nAC_EN,
  output GCLK,
  output out_4,
  output out_5,
  output PC_CLK
);

  wire Bin, Bout, button_1_out, CLK1K, CLK1M, CLK2K, CLK4K, CLK16K, CLK32K, CLK64K, CLK125K, CLK250K,
       CLK500K, I0, JMP, LD, monoflop_1_nq, nand_1_out, nB, nJMP, nQD, nRESET_t, nRST, nT1, nT18, nY0, nY2,
       nY3, nY4, nY5, nY6, PC0, PC1, PC2, PC3, PC4, PC5, PC6, PC7, PC8, PC9, PC10, PC11, PC12, PC13, PC14,
       PC15, PC_CARRYIN, PC_CARRYOUT, PC_in, PC_SUM, PCout, QD, RCO, RESET, reset_1_out, RUN, SETC, T17, T18,
       U2_pin9, U4_pin9, U26_pin9, Y0, Y6, Y7;
  wire [2:0] U8_pin14;

  _74595 U26 (
    .pin1(in_9), .pin2(in_8), .pin3(in_7), .pin4(in_10), .pin5(in_11), .pin6(in_12), .pin7(in_13),
    .pin8(1'b0), .pin9(U26_pin9), .pin10(nRESET), .pin11(SCLK), .pin12(STB), .pin13(nRE), .pin14(DATA),
    .pin15(in_22), .pin16(1'b1));
  _74595 U27 (
    .pin1(in_20), .pin2(in_19), .pin3(in_18), .pin4(in_17), .pin5(in_16), .pin6(in_15), .pin7(in_14),
    .pin8(1'b0), .pin10(nRESET), .pin11(SCLK), .pin12(STB), .pin13(nRE), .pin14(U26_pin9), .pin15(in_21),
    .pin16(1'b1));  // open: pin9
  _74HC4060 U6 (
    .nCKin(clk), .CLR(RESET), .Q12(CLK4K), .Q13(CLK2K), .Q14(CLK1K), .Q7(CLK125K), .Q8(CLK64K), .Q9(CLK32K),
    .Q10(CLK16K), .Q4(CLK1M), .Q5(CLK500K), .Q6(CLK250K), .VCC(1'b1), .GND(1'b0));  // open: CKout, nCKout
  _74595 U2 (
    .pin1(PC14), .pin2(PC13), .pin3(PC12), .pin4(PC11), .pin5(PC10), .pin6(PC9), .pin7(PC8), .pin8(1'b0),
    .pin9(U2_pin9), .pin10(nRESET_t), .pin11(PC_CLK), .pin12(nT18), .pin13(1'b0), .pin14(PC_in),
    .pin15(PC15), .pin16(1'b1));
  _74595 U3 (
    .pin1(PC6), .pin2(PC5), .pin3(PC4), .pin4(PC3), .pin5(PC2), .pin6(PC1), .pin7(PC0), .pin8(1'b0),
    .pin9(PCout), .pin10(nRESET_t), .pin11(PC_CLK), .pin12(nT18), .pin13(1'b0), .pin14(U2_pin9), .pin15(PC7),
    .pin16(1'b1));
  nand nand_1 (nand_1_out, clk, clk);
  nand nand_2 (nAC_EN, nT1, nRST);
  nand nand_3 (nRST, nAC_EN, out_5);
  nand nand_4 (PC_CLK, nand_1_out, nAC_EN);
  _74161 U8 (
    .pin1(nAC_EN), .pin2(clk), .pin3(1'b0), .pin4(1'b0), .pin5(1'b0), .pin6(1'b0), .pin7(1'b1), .pin8(1'b0),
    .pin9(1'b1), .pin10(1'b1), .pin11(QD), .pin12(U8_pin14[2]), .pin13(U8_pin14[1]), .pin14(U8_pin14[0]),
    .pin15(RCO), .pin16(1'b1));
  _74165 U4 (
    .pin1(out_4), .pin2(PC_CLK), .pin3(in_10), .pin4(in_11), .pin5(in_12), .pin6(in_13), .pin8(1'b0),
    .pin9(U4_pin9), .pin10(1'b0), .pin11(in_22), .pin12(in_9), .pin13(in_8), .pin14(in_7), .pin15(1'b0),
    .pin16(1'b1));  // open: pin7
  _74165 U5 (
    .pin1(out_4), .pin2(PC_CLK), .pin3(in_17), .pin4(in_16), .pin5(in_15), .pin6(in_14), .pin8(1'b0),
    .pin9(Bout), .pin10(U4_pin9), .pin11(in_21), .pin12(in_20), .pin13(in_19), .pin14(in_18), .pin15(1'b0),
    .pin16(1'b1));  // open: pin7
  Seven_Seg_Hex seven_seg_hex_1 (.d({QD, U8_pin14}), .dp(1'b0));
  _74175 U9 (
    .pin1(nRESET_t), .pin2(T17), .pin3(out_5), .pin4(RCO), .pin5(T17), .pin6(nT18), .pin7(T18), .pin8(1'b0),
    .pin9(clk), .pin10(LD), .pin11(out_4), .pin12(RUN), .pin13(LD), .pin14(nT1), .pin15(SETC), .pin16(1'b1));
  _74283 U14 (
    .pin1(PC_CARRYOUT), .pin2(1'b0), .pin3(1'b0), .pin4(PC_SUM), .pin5(1'b0), .pin6(PCout),
    .pin7(PC_CARRYIN), .pin8(1'b0), .pin11(1'b1), .pin12(1'b1), .pin14(1'b1), .pin15(1'b1), .pin16(1'b1));  // open: pin9, pin10, pin13
  Monoflop monoflop_1 (.C(button_1_out), .R(1'b0), .nQ(monoflop_1_nq));  // open: Q
  Button button_1 (.out(button_1_out));
  _74138 U10 (
    .pin1(in_7), .pin2(in_8), .pin3(in_9), .pin4(1'b0), .pin5(1'b0), .pin6(1'b1), .pin7(nJMP), .pin8(1'b0),
    .pin9(nY6), .pin10(nY5), .pin11(nY4), .pin12(nY3), .pin13(nY2), .pin14(I0), .pin15(nY0), .pin16(1'b1));
  nand nand_5 (RUN, nT18, monoflop_1_nq);
  Seven_Seg_Hex seven_seg_hex_2 (.d({PC15, PC14, PC13, PC12}), .dp(1'b0));
  and and_1 (GCLK, 1'b1, nQD, PC_CLK);
  Seven_Seg_Hex seven_seg_hex_3 (.d({PC11, PC10, PC9, PC8}), .dp(1'b0));
  Seven_Seg_Hex seven_seg_hex_4 (.d({PC7, PC6, PC5, PC4}), .dp(1'b0));
  _74126 U15 (
    .pin1(1'b1), .pin2(1'b1), .pin4(1'b1), .pin5(1'b1), .pin7(1'b0), .pin8(PC_in), .pin9(Bout), .pin10(JMP),
    .pin11(PC_in), .pin12(PC_SUM), .pin13(nJMP), .pin14(1'b1));  // open: pin3, pin6
  Seven_Seg_Hex seven_seg_hex_5 (.d({PC3, PC2, PC1, PC0}), .dp(1'b0));
  xor xor_1 (Y7, 1'b1, nJMP);
  xor xor_2 (Y0, 1'b1, nY0);
  xor xor_3 (Bin, Bout, nB);
  xor xor_4 (nB, 1'b1, nY5);
  Seven_Seg_Hex seven_seg_hex_6 (.d({in_22, in_9, in_8, in_7}), .dp(1'b0));
  Seven_Seg_Hex seven_seg_hex_7 (.d({in_10, in_11, in_12, in_13}), .dp(1'b0));
  Seven_Seg_Hex seven_seg_hex_8 (.d({in_21, in_20, in_19, in_18}), .dp(1'b0));
  _7474 U16 (
    .pin1(1'b1), .pin2(1'b1), .pin3(1'b1), .pin4(1'b1), .pin7(1'b0), .pin9(PC_CARRYIN), .pin10(out_4),
    .pin11(GCLK), .pin12(PC_CARRYOUT), .pin13(1'b1), .pin14(1'b1));  // open: pin5, pin6, pin8
  Seven_Seg_Hex seven_seg_hex_9 (.d({in_17, in_16, in_15, in_14}), .dp(1'b0));
  Reset reset_1 (.out(reset_1_out));
  not not_1 (Y6, nY6);
  not not_2 (nQD, QD);
  not not_3 (RESET, reset_1_out);
  not not_4 (JMP, nJMP);
  not not_5 (nRESET_t, RESET);

  // Other names for the same wires on the sheet: CLK16 = clk; IR0 = in_13; IR1 = in_12; IR2 = in_11; IR3 = in_10;
  //   IR4 = in_7; IR5 = in_8; IR6 = in_9; IR7 = in_22; nLOADB = out_4; nT0 = out_4; nT17 = out_5; RCLK = out_5;
  //   nY1 = I0; nY7 = nJMP; D0 = in_14; P0 = in_14; D1 = in_15; P1 = in_15; D2 = in_16; P2 = in_16; D3 = in_17;
  //   P3 = in_17; D4 = in_18; P4 = in_18; D5 = in_19; P5 = in_19; D6 = in_20; P6 = in_20; D7 = in_21; P7 = in_21;
  //   RST = nAC_EN; T0 = LD; T1 = SETC

  // Notes on the sheet:
  //   clk: Hz: 100
  //   nRE: default 1
  //   TICK 8-BIT SERIAL COMPUTER - STAGE 3: PI PICO  "ROMULATOR"
  //   BUILD STEPS - STAGE 3.
  //   1. Add sockets for U26 and U27. Solder in 100nF capacitors C26, and C27.
  //   2. Solder in 2x20 way female header J3 on LHS of PCB. Solder the 6 pin male pin header into the "ROMULATOR IN" position X2
  //   3. Solder the 2 yellow, 20 way male pin headers onto the "Pi Pico" module. NOTE!! The LH header with GPIO 0:15 is on the underside of the module.  The RH "power" header is on the topside..
  //   4. Insert ICs U26, U27
  //   5. Load the Pi Pico with the "ROMULATOR-1" sketch. Fit the Pi Pico into J3.
  //   6. Using 3 off, DuPont female/female jumper leads connect Pico GPIO pins (18) (19) (20) to X2 pins (3) (4) (5)
  //   ROMULATOR
  //   TIMING SEQUENCER
  //   X2
  //   1
  //   2
  //   3
  //   4
  //   PROGRAM COUNTER
  //   U7
  //   ALU & PROGRAM COUNTER
  //   5
  //   12
  //   13
  //   6
  //   U7D
  //   U7A
  //   U7B
  //   10
  //   11
  //   U7C
  //   9
  //   8
  //   B-REGISTER
  //   B-REGISTER H
  //   B-REGISTER L
  //   # Clock
  //   SEQUENCER FFs
  //   NOT INCLUDED ON PCB
  //   INSTRUCTION DECODER
  //   STEP/RUN
  //   U11
  //   74HC11
  //   U11C
  //   ROM ADDRESS
  //   PC / ALU MUX
  //   U12
  //   U12B
  //   U12C
  //   U12D
  //   INSTR.      DATA
  //   U12A
  //   Carry FF
  //   PC Carry FF
  //   INVERTERS/RESET
  //   RESET
  //   U19A
  //   U19
  //   U19B
  //   U19C
  //   U19E
  //   U19F
  //   U19D
endmodule
