// Digital circuit TICK_04.dig as structural Verilog
module TICK_04 (
  input  clk,
  input  S1,
  input  nD__gt_BUS,
  input  in_16,
  input  S_nR,
  input  IR7,
  input  IR6,
  input  IR5,
  input  IR4,
  input  IR3,
  input  IR2,
  input  IR1,
  input  IR0,
  input  in_27,
  input  P0,
  input  P1,
  input  P2,
  input  P3,
  input  P4,
  input  P5,
  input  P6,
  input  P7,
  output LD,
  output nRES,
  output GCLK,
  output T0,
  output nRST,
  output PC_CLK,
  output nCRES,
  output nCSET,
  output I2,
  output I3,
  output nB,
  output nCLR,
  output T1,
  output LOAD_nSHIFT
);

  wire ALU_CARRY, ALU_SUM, and_1_out, Aout, BCC, BCC_JMP, Bout, BUS0, BUS1, BUS2, BUS3, BUS4, BUS5, BUS6,
       BUS7, button_1_out, button_2_out, button_3_out, button_4_out, button_5_out, button_6_out,
       button_7_out, button_8_out, button_9_out, CARRY, Cin, D0, D1, D2, D3, D4, D5, D6, D7, d_ff_1_nq,
       d_ff_2_nq, d_ff_3_nq, d_ff_4_nq, d_ff_5_nq, d_ff_6_nq, diodeforward_3_out, Fout, IC16_2_nq, IC16_nq,
       JMP, LONGJUMP, MA8, MA9, MA10, MA11, MA12, MA13, MA14, monoflop_1_q, MOSI, nand_10_out, nCE, nCSup,
       nJMP, not_1_out, not_2_out, not_3_out, not_4_out, nQD, nRD, nRESET, nRESETSR, nT18, nWR, nY0, nY2,
       nY3, nY4, nY5, nY6, or_1_out, PC0, PC1, PC2, PC3, PC4, PC5, PC6, PC7, PC8, PC9, PC10, PC11, PC12,
       PC13, PC14, PC15, PC_CARRYIN, PC_CARRYOUT, PC_DATA_IN, PC_in, PCout, pulldown_1_out, QD, RCO, RESET,
       RST, RUN, T17, T18, U2_pin9, U5_pin9, U14_pin14, U15_pin8, U15_pin11, Y0, Y6, ZERO, Zin;
  wire [2:0] U8_pin12;

  PullDown pulldown_1 (.out(pulldown_1_out));
  assign MOSI = ~pulldown_1_out ? Aout : 1'bz;  // DriverInvSel driverinvsel_1
  assign MA14 = ~IR7 ? IR6 : 1'bz;  // DriverInvSel driverinvsel_2
  assign MA13 = ~IR7 ? IR5 : 1'bz;  // DriverInvSel driverinvsel_3
  assign MA12 = ~IR7 ? IR4 : 1'bz;  // DriverInvSel driverinvsel_4
  assign MA11 = ~IR7 ? IR3 : 1'bz;  // DriverInvSel driverinvsel_5
  assign MA10 = ~IR7 ? IR2 : 1'bz;  // DriverInvSel driverinvsel_6
  assign MA9 = ~IR7 ? IR1 : 1'bz;  // DriverInvSel driverinvsel_7
  assign MA8 = ~IR7 ? IR0 : 1'bz;  // DriverInvSel driverinvsel_8
  PullDown pulldown_2 (.out(MA14));
  PullDown pulldown_3 (.out(MA11));
  PullDown pulldown_4 (.out(MA13));
  PullDown pulldown_5 (.out(MA10));
  PullDown pulldown_6 (.out(MA12));
  PullDown pulldown_7 (.out(MA9));
  PullDown pulldown_8 (.out(MA8));
  _7404 U19 (
    .pin1(nY6), .pin2(Y6), .pin3(QD), .pin4(nQD), .pin5(nRESET), .pin6(RESET), .pin7(1'b0), .pin8(JMP),
    .pin9(nJMP), .pin10(LOAD_nSHIFT), .pin11(nCE), .pin13(1'b1), .pin14(1'b1));  // open: pin12
  nand nand_1 (nRD, LD, Y0);
  nand nand_2 (nWR, T17, Y6);
  nand nand_3 (LONGJUMP, JMP, IR3);
  nand nand_4 (nCE, T1, Y0);
  LED led_1 (.in(BCC_JMP));
  not not_1 (not_1_out, nJMP);
  Monoflop monoflop_1 (.C(button_1_out), .R(1'b0), .Q(monoflop_1_q));  // open: nQ
  Button button_1 (.out(button_1_out));
  nand nand_5 (LONGJUMP, not_1_out, IR3);
  Seven_Seg_Hex seven_seg_hex_1 (.d({1'b0, MA14, MA13, MA12}), .dp(1'b0));
  Seven_Seg_Hex seven_seg_hex_2 (.d({PC15, PC14, PC13, PC12}), .dp(1'b0));
  Reset reset_1 (.out(nRESET));
  Multiplexer multiplexer_1 (.sel(S_nR), .in_0(T18), .in_1(monoflop_1_q), .out(RUN));
  _74138 U10 (
    .pin1(IR4), .pin2(IR5), .pin3(IR6), .pin4(1'b0), .pin5(1'b0), .pin6(1'b1), .pin7(nJMP), .pin8(1'b0),
    .pin9(nY6), .pin10(nY5), .pin11(nY4), .pin12(nY3), .pin13(nY2), .pin14(I2), .pin15(nY0), .pin16(1'b1));
  Seven_Seg_Hex seven_seg_hex_3 (.d({MA11, MA10, MA9, MA8}), .dp(1'b0));
  Seven_Seg_Hex seven_seg_hex_4 (.d({PC11, PC10, PC9, PC8}), .dp(1'b0));
  Seven_Seg_Hex seven_seg_hex_5 (.d({P7, P6, P5, P4}), .dp(1'b0));
  Seven_Seg_Hex seven_seg_hex_6 (.d({PC7, PC6, PC5, PC4}), .dp(1'b0));
  LED led_2 (.in(D7));
  D_FF IC16 (.D(IC16_nq), .C(button_2_out), .Q(D7), .nQ(IC16_nq));
  Seven_Seg_Hex seven_seg_hex_7 (.d({P3, P2, P1, P0}), .dp(1'b0));
  Seven_Seg_Hex seven_seg_hex_8 (.d({PC3, PC2, PC1, PC0}), .dp(1'b0));
  LED led_3 (.in(D6));
  D_FF d_ff_1 (.D(d_ff_1_nq), .C(button_3_out), .Q(D6), .nQ(d_ff_1_nq));
  Button button_2 (.out(button_2_out));
  LED led_4 (.in(D5));
  D_FF d_ff_2 (.D(d_ff_2_nq), .C(button_4_out), .Q(D5), .nQ(d_ff_2_nq));
  Button button_3 (.out(button_3_out));
  xor xor_1 (nB, 1'b1, nY5);
  xor xor_2 (Y0, 1'b1, nY0);
  Seven_Seg_Hex seven_seg_hex_9 (.d({BUS7, BUS6, BUS5, BUS4}), .dp(1'b0));
  Seven_Seg_Hex seven_seg_hex_10 (.d({IR7, IR6, IR5, IR4}), .dp(1'b0));
  LED led_5 (.in(D4));
  D_FF d_ff_3 (.D(d_ff_3_nq), .C(button_5_out), .Q(D4), .nQ(d_ff_3_nq));
  Button button_4 (.out(button_4_out));
  Seven_Seg_Hex seven_seg_hex_11 (.d({BUS3, BUS2, BUS1, BUS0}), .dp(1'b0));
  Seven_Seg_Hex seven_seg_hex_12 (.d({IR3, IR2, IR1, IR0}), .dp(1'b0));
  LED led_6 (.in(D3));
  D_FF d_ff_4 (.D(d_ff_4_nq), .C(button_6_out), .Q(D3), .nQ(d_ff_4_nq));
  Button button_5 (.out(button_5_out));
  nand nand_6 (nCSup, T0, nY5);
  nand nand_7 (nCSET, nB, T1);
  nand nand_8 (I3, I2, nY2);
  nand nand_9 (nCLR, T0, Y0);
  and and_1 (and_1_out, I2, nY2, nY3);
  Seven_Seg_Hex seven_seg_hex_13 (.d({P7, P6, P5, P4}), .dp(1'b0));
  LED led_7 (.in(D2));
  D_FF d_ff_5 (.D(d_ff_5_nq), .C(button_7_out), .Q(D2), .nQ(d_ff_5_nq));
  Button button_6 (.out(button_6_out));
  Seven_Seg_Hex seven_seg_hex_14 (.d({P3, P2, P1, P0}), .dp(1'b0));
  LED led_8 (.in(D1));
  D_FF d_ff_6 (.D(d_ff_6_nq), .C(button_8_out), .Q(D1), .nQ(d_ff_6_nq));
  Button button_7 (.out(button_7_out));
  and and_2 (nCRES, 1'b1, and_1_out, nCSup);
  LED led_9 (.in(D0));
  D_FF IC16_2 (.D(IC16_2_nq), .C(button_9_out), .Q(D0), .nQ(IC16_2_nq));
  Button button_8 (.out(button_8_out));
  Seven_Seg_Hex seven_seg_hex_15 (.d({D7, D6, D5, D4}), .dp(1'b0));
  Button button_9 (.out(button_9_out));
  Seven_Seg_Hex seven_seg_hex_16 (.d({D3, D2, D1, D0}), .dp(1'b0));
  _74165 U5 (
    .pin1(LD), .pin2(GCLK), .pin3(IR3), .pin4(IR2), .pin5(IR1), .pin6(IR0), .pin8(1'b0), .pin9(U5_pin9),
    .pin10(1'b0), .pin11(IR7), .pin12(IR6), .pin13(IR5), .pin14(IR4), .pin15(1'b0), .pin16(1'b1));  // open: pin7
  nand nand_10 (nand_10_out, clk, clk);
  nand nand_11 (RST, nRES, nRST);
  nand nand_12 (nRST, RST, nRESETSR);
  nand nand_13 (PC_CLK, nand_10_out, RST);
  not not_2 (not_2_out, nJMP);
  _74165 U4 (
    .pin1(LD), .pin2(GCLK), .pin3(D3), .pin4(D2), .pin5(D1), .pin6(D0), .pin8(1'b0), .pin9(Bout),
    .pin10(U5_pin9), .pin11(D7), .pin12(D6), .pin13(D5), .pin14(D4), .pin15(1'b0), .pin16(1'b1));  // open: pin7
  _74126 U15 (
    .pin1(nJMP), .pin2(PC_DATA_IN), .pin3(PC_in), .pin4(not_2_out), .pin5(Bout), .pin6(PC_in), .pin7(1'b0),
    .pin8(U15_pin8), .pin9(ALU_CARRY), .pin10(I3), .pin11(U15_pin11), .pin12(ALU_SUM), .pin13(I2),
    .pin14(1'b1));
  _74283 U14 (
    .pin1(PC_CARRYOUT), .pin2(1'b0), .pin3(1'b0), .pin4(PC_DATA_IN), .pin5(1'b0), .pin6(PCout),
    .pin7(PC_CARRYIN), .pin8(1'b0), .pin9(ALU_CARRY), .pin10(ALU_SUM), .pin11(Cin), .pin12(Aout),
    .pin14(U14_pin14), .pin15(1'b1), .pin16(1'b1));  // open: pin13
  not not_3 (not_3_out, QD);
  and and_3 (GCLK, 1'b1, not_3_out, PC_CLK);
  DiodeForward diodeforward_1 (.in(U15_pin11), .out(Fout));
  DiodeForward diodeforward_2 (.in(U15_pin8), .out(Fout));
  _74161 U8 (
    .pin1(RST), .pin2(clk), .pin3(1'b0), .pin4(1'b0), .pin5(1'b0), .pin6(1'b0), .pin7(1'b1), .pin8(1'b0),
    .pin9(1'b1), .pin10(1'b1), .pin11(QD), .pin12(U8_pin12[2]), .pin13(U8_pin12[1]), .pin14(U8_pin12[0]),
    .pin15(RCO), .pin16(1'b1));
  PullDown pulldown_9 (.out(Fout));
  xor xor_3 (U14_pin14, Bout, nB);
  _74299 U17 (
    .pin1(LOAD_nSHIFT), .pin2(RST), .pin3(RST), .pin4(BUS6), .pin5(BUS4), .pin6(BUS2), .pin7(BUS0),
    .pin8(Aout), .pin9(nCLR), .pin10(1'b0), .pin11(1'b0), .pin12(GCLK), .pin13(BUS1), .pin14(BUS3),
    .pin15(BUS5), .pin16(BUS7), .pin18(Fout), .pin19(S1), .pin20(1'b1));  // open: pin17
  LED led_10 (.in(ZERO));
  _7474 U16 (
    .pin1(nCRES), .pin2(ALU_CARRY), .pin3(GCLK), .pin4(nCSET), .pin5(Cin), .pin7(1'b0), .pin9(PC_CARRYIN),
    .pin10(LD), .pin11(GCLK), .pin12(PC_CARRYOUT), .pin13(1'b1), .pin14(1'b1));  // open: pin6, pin8
  _7474 U22 (
    .pin1(1'b1), .pin2(Zin), .pin3(clk), .pin4(1'b1), .pin5(ZERO), .pin7(1'b0), .pin9(CARRY), .pin10(1'b1),
    .pin11(clk), .pin12(1'b1), .pin13(1'b1), .pin14(1'b1));  // open: pin6, pin8
  Seven_Seg_Hex seven_seg_hex_17 (.d({QD, U8_pin12}), .dp(1'b0));
  LED led_11 (.in(CARRY));
  LED led_12 (.in(BCC_JMP));
  // _27C1024 U1: pin names not known; wires that end beside it: 1'b1, in_27, IR7, IR6, IR5, IR4, IR3, IR2, IR1, IR0, 1'b0, P7, P6, P5, 1'b1, PC15, PC14, PC13, PC12, PC11, PC10, PC9
  // _62256 U18: pin names not known; wires that end beside it: P4, P3, P2, P1, P0, 1'b0, MA14, MA12, P7, P6, P5, P4, P3, P2, P1, P0, BUS0, BUS1, BUS2, 1'b0, PC2, PC1, PC0, 1'b1, nWR, MA13, MA8, MA9, MA11, nRD, MA10, nCE, BUS7
  _74175 U9 (
    .pin1(nRESET), .pin2(T17), .pin3(nRESETSR), .pin4(RCO), .pin5(T17), .pin6(nT18), .pin7(T18), .pin8(1'b0),
    .pin9(clk), .pin10(T0), .pin11(LD), .pin12(RUN), .pin13(T0), .pin14(nRES), .pin15(T1), .pin16(1'b1));
  and and_4 (BCC_JMP, LONGJUMP, or_1_out);
  or or_1 (or_1_out, nJMP, not_4_out);
  not not_4 (not_4_out, BCC);
  _74153 U23 (
    .pin1(nJMP), .pin2(BUS7), .pin3(1'b0), .pin4(IR2), .pin5(IR1), .pin6(IR0), .pin7(BCC), .pin8(1'b0),
    .pin10(1'b0), .pin11(1'b0), .pin12(1'b0), .pin13(1'b0), .pin14(ZERO), .pin15(1'b0), .pin16(1'b1));  // open: pin9
  _74595 U2 (
    .pin1(PC14), .pin2(PC13), .pin3(PC12), .pin4(PC11), .pin5(PC10), .pin6(PC9), .pin7(PC8), .pin8(1'b0),
    .pin9(U2_pin9), .pin10(nRESET), .pin11(PC_CLK), .pin12(nRESETSR), .pin13(1'b0), .pin14(PC_in),
    .pin15(PC15), .pin16(1'b1));
  _74595 U3 (
    .pin1(PC6), .pin2(PC5), .pin3(PC4), .pin4(PC3), .pin5(PC2), .pin6(PC1), .pin7(PC0), .pin8(1'b0),
    .pin9(PCout), .pin10(nRESET), .pin11(PC_CLK), .pin12(nRESETSR), .pin13(1'b0), .pin14(U2_pin9),
    .pin15(PC7), .pin16(1'b1));
  DiodeForward diodeforward_3 (.in(BUS7), .out(diodeforward_3_out));
  DiodeForward diodeforward_4 (.in(BUS6), .out(diodeforward_3_out));
  DiodeForward diodeforward_5 (.in(BUS5), .out(diodeforward_3_out));
  DiodeForward diodeforward_6 (.in(BUS4), .out(diodeforward_3_out));
  DiodeForward diodeforward_7 (.in(BUS3), .out(diodeforward_3_out));
  DiodeForward diodeforward_8 (.in(BUS2), .out(diodeforward_3_out));
  DiodeForward diodeforward_9 (.in(BUS1), .out(diodeforward_3_out));
  DiodeForward diodeforward_10 (.in(BUS0), .out(diodeforward_3_out));
  PullDown pulldown_10 (.out(diodeforward_3_out));
  xor xor_4 (Zin, 1'b1, diodeforward_3_out);

  // Other names for the same wires on the sheet: D_BUS = nD__gt_BUS; I1 = I3; LD_t = T0; nRAMCE = in_16; nLOADB = LD;
  //   nT0 = LD; nSETSR = nRES; nT1 = nRES; nT17 = nRESETSR; RCLK = nRESETSR; I0 = I2; nY1 = I2; nY7 = nJMP;
  //   S0 = LOAD_nSHIFT; SETC = T1

  // Notes on the sheet:
  //   clk: Hz: 5
  //   S1: default 1
  //   nD__gt_BUS: default 1
  //   in_16: default 1
  //   S_nR: default 1
  //   in_27: default 1
  //   SUPPRESS TOP ADDRESS LINES
  //   U24
  //   READ RAM
  //   WRITE TO RAM
  //   WRITE TO AC
  //   TICK 04
  //   INSTRUCTION DECODER
  //   DATA INPUT
  //   RAM ADDRESS
  //   ROM ADDRESS
  //   STEP/RUN
  //   U12B
  //   U12C
  //   AC / BUS
  //   INSTR.      DATA
  //   Suppress Carry
  //   74HC00
  //   74HC11
  //   U11A
  //   U13
  //   U11B
  //   SWITCHES
  //   REGISTERS
  //   CLOCK SEQUENCER
  //   ALU
  //   U7
  //   16 bit Shift Register B
  //   B-REGISTER
  //   TICK 8-bit  Bit serial CPU Testbed
  //   PC / ALU MUX
  //   U11C
  //   U12D
  //   ACCUMULATOR
  //   Carry FF
  //   # Clock
  //   ZERO/CARRY FFs
  //   PC Carry FF
  //   PROGRAM COUNTER ROM & RAM
  //   SEQUENCER FFs
  //   BRANCH CONDITION
  //   U12A
  //   Zero Detect
endmodule
