// Digital circuit TICK_schematic_2.dig as structural Verilog
module TICK_schematic_2 (
  input  clk,
  input  in_7,
  input  in_8,
  input  in_9,
  input  in_10,
  input  in_11,
  input  in_12,
  input  in_13,
  input  in_14,
  input  in_15,
  input  in_16,
  input  in_17,
  input  in_18,
  input  in_19,
  input  in_20,
  input  in_21,
  input  in_22,
  input  DATA,
  input  STB,
  input  SCLK,
  input  nRE,
  input  nRESET,
  input  in_43,
  input  in_44,
  input  nIE,
  output nCE,
  output nOE,
  output nWE,
  output nAC_EN,
  output GCLK,
  output out_23,
  output out_24,
  output out_25,
  output out_26,
  output out_27,
  output out_28,
  output PC_CLK,
  output PC0,
  output PC1,
  output PC2,
  output PC3,
  output PC4,
  output PC5,
  output PC6,
  output PC7
);

  wire ALU_CARRY, ALU_SUM, Aout, BCC, BCC_JMP, Bin, Bout, BUS0, BUS1, BUS2, BUS3, BUS4, BUS5, BUS6, BUS7,
       button_1_out, CARRY, Cin, CLK1K, CLK1M, CLK2K, CLK4K, CLK16K, CLK32K, CLK64K, CLK125K, CLK250K,
       CLK500K, Fout, I0, I1, JMP, LONGJUMP, MA8, monoflop_1_nq, MOSI, nand_2_out, nand_16_out, nand_17_out,
       nB, nCE_t, nCLR, nCRES, nCSET, nCSup, nF, nJMP, nOE_t, nQD, nRESET_t, nRST, nWE_t, nY0, nY2, nY3, nY4,
       nY5, nY6, nZin, PC8, PC9, PC10, PC11, PC12, PC13, PC14, PC15, PC_CARRYIN, PC_CARRYOUT, PC_in, PC_SUM,
       PCout, pulldown_9_out, QD, RCO, RESET, reset_1_out, RUN, S0, U2_pin9, U4_pin9, U15_pin3, U15_pin6,
       U22_pin9, U26_pin9, Y0, Y6, Y7, Zin, Zout;
  wire [2:0] U8_pin14;

  Monoflop monoflop_1 (.C(button_1_out), .R(1'b0), .nQ(monoflop_1_nq));  // open: Q
  Button button_1 (.out(button_1_out));
  // _27C1024 U1: pin names not known; wires that end beside it: 1'b1, in_43, in_22, in_9, in_8, in_7, in_10, in_11, in_12, in_13, 1'b0, in_21, in_20, in_19, in_18, in_17, 1'b1, PC15, PC14, PC13, PC12, PC11, PC10, PC9
  and and_1 (nCE, nOE, nWE);
  nand nand_1 (RUN, nWE, monoflop_1_nq);
  _74595 U26 (
    .pin1(in_9), .pin2(in_8), .pin3(in_7), .pin4(in_10), .pin5(in_11), .pin6(in_12), .pin7(in_13),
    .pin8(1'b0), .pin9(U26_pin9), .pin10(nRESET), .pin11(SCLK), .pin12(STB), .pin13(nRE), .pin14(DATA),
    .pin15(in_22), .pin16(1'b1));
  _74595 U27 (
    .pin1(in_20), .pin2(in_19), .pin3(in_18), .pin4(in_17), .pin5(in_16), .pin6(in_15), .pin7(in_14),
    .pin8(1'b0), .pin10(nRESET), .pin11(SCLK), .pin12(STB), .pin13(nRE), .pin14(U26_pin9), .pin15(in_21),
    .pin16(1'b1));  // open: pin9
  _74HC4060 U6 (
    .nCKin(clk), .CLR(RESET), .Q12(CLK4K), .Q13(CLK2K), .Q14(CLK1K), .Q7(CLK125K), .Q8(CLK64K), .Q9(CLK32K),
    .Q10(CLK16K), .Q4(CLK1M), .Q5(CLK500K), .Q6(CLK250K), .VCC(1'b1), .GND(1'b0));  // open: CKout, nCKout
  _74153 U23 (
    .pin1(nJMP), .pin2(BUS7), .pin3(1'b0), .pin4(in_11), .pin5(in_12), .pin6(in_13), .pin7(BCC), .pin8(1'b0),
    .pin10(1'b0), .pin11(1'b0), .pin12(1'b0), .pin13(1'b0), .pin14(Zin), .pin15(1'b0), .pin16(1'b1));  // open: pin9
  _74595 U2 (
    .pin1(PC14), .pin2(PC13), .pin3(PC12), .pin4(PC11), .pin5(PC10), .pin6(PC9), .pin7(PC8), .pin8(1'b0),
    .pin9(U2_pin9), .pin10(nRESET_t), .pin11(PC_CLK), .pin12(nWE), .pin13(1'b0), .pin14(PC_in), .pin15(PC15),
    .pin16(1'b1));
  _74595 U3 (
    .pin1(PC6), .pin2(PC5), .pin3(PC4), .pin4(PC3), .pin5(PC2), .pin6(PC1), .pin7(PC0), .pin8(1'b0),
    .pin9(PCout), .pin10(nRESET_t), .pin11(PC_CLK), .pin12(nWE), .pin13(1'b0), .pin14(U2_pin9), .pin15(PC7),
    .pin16(1'b1));
  nand nand_2 (nand_2_out, clk, clk);
  nand nand_3 (nAC_EN, nOE, nRST);
  nand nand_4 (nRST, nAC_EN, out_28);
  nand nand_5 (PC_CLK, nand_2_out, nAC_EN);
  _74161 U8 (
    .pin1(nAC_EN), .pin2(clk), .pin3(1'b0), .pin4(1'b0), .pin5(1'b0), .pin6(1'b0), .pin7(1'b1), .pin8(1'b0),
    .pin9(1'b1), .pin10(1'b1), .pin11(QD), .pin12(U8_pin14[2]), .pin13(U8_pin14[1]), .pin14(U8_pin14[0]),
    .pin15(RCO), .pin16(1'b1));
  nand nand_6 (nOE_t, out_27, Y0);
  nand nand_7 (nWE_t, out_25, Y6);
  nand nand_8 (nCE_t, out_24, Y0);
  nand nand_9 (nZin, Zin, Zin);
  _74165 U4 (
    .pin1(out_27), .pin2(GCLK), .pin3(in_10), .pin4(in_11), .pin5(in_12), .pin6(in_13), .pin8(1'b0),
    .pin9(U4_pin9), .pin10(1'b0), .pin11(in_22), .pin12(in_9), .pin13(in_8), .pin14(in_7), .pin15(1'b0),
    .pin16(1'b1));  // open: pin7
  _74165 U5 (
    .pin1(out_27), .pin2(GCLK), .pin3(in_17), .pin4(in_16), .pin5(in_15), .pin6(in_14), .pin8(1'b0),
    .pin9(Bout), .pin10(U4_pin9), .pin11(in_21), .pin12(in_20), .pin13(in_19), .pin14(in_18), .pin15(1'b0),
    .pin16(1'b1));  // open: pin7
  Seven_Seg_Hex seven_seg_hex_1 (.d({QD, U8_pin14}), .dp(1'b0));
  _74175 U9 (
    .pin1(nRESET_t), .pin2(out_25), .pin3(out_28), .pin4(RCO), .pin5(out_25), .pin6(nWE), .pin7(out_26),
    .pin8(1'b0), .pin9(clk), .pin10(out_23), .pin11(out_27), .pin12(RUN), .pin13(out_23), .pin14(nOE),
    .pin15(out_24), .pin16(1'b1));
  _74283 U14 (
    .pin1(PC_CARRYOUT), .pin2(1'b0), .pin3(1'b0), .pin4(PC_SUM), .pin5(1'b0), .pin6(PCout),
    .pin7(PC_CARRYIN), .pin8(1'b0), .pin9(ALU_CARRY), .pin10(ALU_SUM), .pin11(Cin), .pin12(Aout),
    .pin14(Bin), .pin15(1'b1), .pin16(1'b1));  // open: pin13
  Seven_Seg_Hex seven_seg_hex_2 (.d({PC15, PC14, PC13, PC12}), .dp(1'b0));
  assign MA8 = ~in_22 ? in_10 : 1'bz;  // DriverInvSel driverinvsel_1
  assign MA8 = ~in_22 ? in_11 : 1'bz;  // DriverInvSel driverinvsel_2
  assign MA8 = ~in_22 ? in_12 : 1'bz;  // DriverInvSel driverinvsel_3
  assign MA8 = ~in_22 ? in_13 : 1'bz;  // DriverInvSel driverinvsel_4
  _74299 U17 (
    .pin1(nAC_EN), .pin2(out_28), .pin3(out_28), .pin4(BUS6), .pin5(BUS4), .pin6(BUS2), .pin7(BUS0),
    .pin8(Aout), .pin9(nCLR), .pin10(1'b0), .pin11(1'b0), .pin12(GCLK), .pin13(BUS1), .pin14(BUS3),
    .pin15(BUS5), .pin16(BUS7), .pin18(Fout), .pin19(1'b1), .pin20(1'b1));  // open: pin17
  Seven_Seg_Hex seven_seg_hex_3 (.d({PC11, PC10, PC9, PC8}), .dp(1'b0));
  PullDown pulldown_1 (.out(MA8));
  PullDown pulldown_2 (.out(MA8));
  Seven_Seg_Hex seven_seg_hex_4 (.d({PC7, PC6, PC5, PC4}), .dp(1'b0));
  PullDown pulldown_3 (.out(MA8));
  PullDown pulldown_4 (.out(MA8));
  LED led_1 (.in(Zout));
  Seven_Seg_Hex seven_seg_hex_5 (.d({PC3, PC2, PC1, PC0}), .dp(1'b0));
  _74138 U10 (
    .pin1(in_7), .pin2(in_8), .pin3(in_9), .pin4(1'b0), .pin5(1'b0), .pin6(1'b1), .pin7(nJMP), .pin8(1'b0),
    .pin9(nY6), .pin10(nY5), .pin11(nY4), .pin12(nY3), .pin13(nY2), .pin14(I0), .pin15(nY0), .pin16(1'b1));
  _7474 _7474_1 (
    .pin1(1'b1), .pin2(nZin), .pin3(clk), .pin4(1'b1), .pin5(Zout), .pin7(1'b0), .pin9(CARRY), .pin10(1'b1),
    .pin11(clk), .pin12(1'b1), .pin13(1'b1), .pin14(1'b1));  // open: pin6, pin8
  Seven_Seg_Hex seven_seg_hex_6 (.d({in_22, in_9, in_8, in_7}), .dp(1'b0));
  Seven_Seg_Hex seven_seg_hex_7 (.d({in_10, in_11, in_12, in_13}), .dp(1'b0));
  Seven_Seg_Hex seven_seg_hex_8 (.d({in_21, in_20, in_19, in_18}), .dp(1'b0));
  _74595 U22 (
    .pin1(BUS6), .pin2(BUS5), .pin3(BUS4), .pin4(BUS3), .pin5(BUS2), .pin6(BUS1), .pin7(BUS0), .pin8(1'b0),
    .pin9(U22_pin9), .pin10(nRESET_t), .pin11(GCLK), .pin12(nWE), .pin13(nIE), .pin14(in_44), .pin15(BUS7),
    .pin16(1'b1));
  and and_2 (nF, I0, nY2, nY3);
  and and_3 (nCRES, 1'b1, nF, nCSup);
  and and_4 (GCLK, 1'b1, nQD, PC_CLK);
  Seven_Seg_Hex seven_seg_hex_9 (.d({in_17, in_16, in_15, in_14}), .dp(1'b0));
  assign MOSI = ~pulldown_9_out ? Aout : 1'bz;  // DriverInvSel driverinvsel_5
  assign MA8 = ~in_22 ? in_9 : 1'bz;  // DriverInvSel driverinvsel_6
  assign MA8 = ~in_22 ? in_8 : 1'bz;  // DriverInvSel driverinvsel_7
  assign MA8 = ~in_22 ? in_7 : 1'bz;  // DriverInvSel driverinvsel_8
  PullDown pulldown_5 (.out(Fout));
  Seven_Seg_Hex seven_seg_hex_10 (.d({4{MA8}}), .dp(1'b0));
  PullDown pulldown_6 (.out(MA8));
  _74126 U15 (
    .pin1(I0), .pin2(ALU_SUM), .pin3(U15_pin3), .pin4(I1), .pin5(ALU_CARRY), .pin6(U15_pin6), .pin7(1'b0),
    .pin8(PC_in), .pin9(Bout), .pin10(JMP), .pin11(PC_in), .pin12(PC_SUM), .pin13(nJMP), .pin14(1'b1));
  DiodeForward diodeforward_1 (.in(U15_pin3), .out(Fout));
  DiodeForward diodeforward_2 (.in(U15_pin6), .out(Fout));
  Seven_Seg_Hex seven_seg_hex_11 (.d({4{MA8}}), .dp(1'b0));
  PullDown pulldown_7 (.out(MA8));
  PullDown pulldown_8 (.out(MA8));
  Seven_Seg_Hex seven_seg_hex_12 (.d({in_21, in_20, in_19, in_18}), .dp(1'b0));
  PullDown pulldown_9 (.out(pulldown_9_out));
  xor xor_1 (Y7, 1'b1, nJMP);
  xor xor_2 (Y0, 1'b1, nY0);
  xor xor_3 (Bin, Bout, nB);
  xor xor_4 (nB, 1'b1, nY5);
  Seven_Seg_Hex seven_seg_hex_13 (.d({in_17, in_16, in_15, in_14}), .dp(1'b0));
  Seven_Seg_Hex seven_seg_hex_14 (.d({BUS7, BUS6, BUS5, BUS4}), .dp(1'b0));
  Seven_Seg_Hex seven_seg_hex_15 (.d({BUS3, BUS2, BUS1, BUS0}), .dp(1'b0));
  // _62256 U18: pin names not known; wires that end beside it: MA8, MA8, in_21, in_20, in_19, in_18, in_17, in_16, in_15, in_14, BUS0, BUS1, BUS2, 1'b0, 1'b1, nWE, MA8, MA8, MA8, MA8, nOE, MA8, nCE, BUS7
  LED D7 (.in(BUS7));
  _7474 U16 (
    .pin1(nCRES), .pin2(ALU_CARRY), .pin3(GCLK), .pin4(nCSET), .pin5(Cin), .pin7(1'b0), .pin9(PC_CARRYIN),
    .pin10(out_27), .pin11(GCLK), .pin12(PC_CARRYOUT), .pin13(1'b1), .pin14(1'b1));  // open: pin6, pin8
  LED D6 (.in(BUS6));
  LED D5 (.in(BUS5));
  nand nand_10 (nCSup, out_23, nY5);
  nand nand_11 (nCLR, out_23, Y0);
  nand nand_12 (I1, I0, nY2);
  nand nand_13 (nCSET, nB, out_24);
  LED D4 (.in(BUS4));
  DiodeForward diodeforward_3 (.in(BUS7), .out(Zin));
  DiodeForward diodeforward_4 (.in(BUS6), .out(Zin));
  DiodeForward diodeforward_5 (.in(BUS5), .out(Zin));
  DiodeForward diodeforward_6 (.in(BUS4), .out(Zin));
  DiodeForward diodeforward_7 (.in(BUS3), .out(Zin));
  DiodeForward diodeforward_8 (.in(BUS2), .out(Zin));
  DiodeForward diodeforward_9 (.in(BUS1), .out(Zin));
  DiodeForward diodeforward_10 (.in(BUS0), .out(Zin));
  LED D3 (.in(BUS3));
  Reset reset_1 (.out(reset_1_out));
  PullDown pulldown_10 (.out(Zin));
  LED D2 (.in(BUS2));
  nand nand_14 (LONGJUMP, JMP, in_10);
  nand nand_15 (BCC_JMP, LONGJUMP, nand_16_out);
  nand nand_16 (nand_16_out, nJMP, nand_17_out);
  nand nand_17 (nand_17_out, BCC, BCC);
  not not_1 (Y6, nY6);
  not not_2 (nQD, QD);
  not not_3 (RESET, reset_1_out);
  not not_4 (JMP, nJMP);
  not not_5 (S0, nCE_t);
  LED D1 (.in(BUS1));
  LED D0 (.in(BUS0));
  not not_6 (nRESET_t, RESET);
  // also tied to GND on the sheet: MA8

  // Other names for the same wires on the sheet: CLK16 = clk; IR0 = in_13; IR1 = in_12; IR2 = in_11; IR3 = in_10;
  //   IR4 = in_7; IR5 = in_8; IR6 = in_9; IR7 = in_22; MA9 = MA8; MA10 = MA8; MA11 = MA8; MA12 = MA8; MA13 = MA8;
  //   MA14 = MA8; MA15 = MA8; MISO = in_44; nRAMCE = nCE; nLOADB = out_27; nT0 = out_27; nRD = nOE; nT1 = nOE;
  //   nT17 = out_28; RCLK = out_28; nT18 = nWE; nWR = nWE; nY1 = I0; nY7 = nJMP; D0 = in_14; P0 = in_14; D1 = in_15;
  //   P1 = in_15; D2 = in_16; P2 = in_16; D3 = in_17; P3 = in_17; D4 = in_18; P4 = in_18; D5 = in_19; P5 = in_19;
  //   D6 = in_20; P6 = in_20; D7 = in_21; P7 = in_21; RST = nAC_EN; LD = out_23; T0 = out_23; SETC = out_24;
  //   T1 = out_24; T17 = out_25; T18 = out_26

  // Notes on the sheet:
  //   clk: Hz: 4
  //   nRE: default 1
  //   in_43: default 1
  //   nIE: default 1
  //   TICK 8-BIT SERIAL COMPUTER
  //   ROM
  //   STEP/RUN
  //   ROMULATOR
  //   TIMING SEQUENCER
  //   PROGRAM COUNTER
  //   U7
  //   ALU & PROGRAM COUNTER
  //   BRANCH CONDITION
  //   12
  //   13
  //   4
  //   5
  //   U7D
  //   U7A
  //   1
  //   2
  //   U7B
  //   10
  //   11
  //   3
  //   6
  //   U7C
  //   9
  //   8
  //   B-REGISTER
  //   B-REGISTER H
  //   B-REGISTER L
  //   U20
  //   # Clock
  //   ADDRESS BUFFER
  //   ACCUMULATOR
  //   SEQUENCER FFs
  //   U25
  //   ROM ADDRESS
  //   SUPPRESS TOP ADDRESS LINES
  //   INSTRUCTION DECODER
  //   ZERO/CARRY FFs
  //   INSTR.      DATA
  //   SPI INPUT
  //   U24
  //   74HC11
  //   U11
  //   U11A
  //   U11B
  //   U11C
  //   RAM ADDRESS
  //   PC / ALU MUX
  //   U12
  //   U12B
  //   U12C
  //   U12D
  //   U12A
  //   AC / BUS
  //   RAM
  //   DATA BUS
  //   Carry FF
  //   U13
  //   U13A
  //   U13D
  //   U13B
  //   U13C
  //   PC Carry FF
  //   Suppress Carry
  //   INVERTERS/RESET
  //   RESET
  //   Zero Detect
  //   U28
  //   U28A
  //   U28C
  //   U19A
  //   U19
  //   U19B
  //   U19C
  //   U19E
  //   U19F
  //   U28B
  //   U28D
  //   U19D
endmodule
